# Fritzing sketch debouncing (saved by Fritzing 0.9.4)
breadboards: 1

parts:
  Parça1 = Arduino Uno (Rev3)
  R1 = Resistor [tolerance=±5% resistance=220 package=THT]
  S1 = Pushbutton [package="[THT]"]

nets:
  N1: Parça1.GND, R1.Pin_1
  N2: Parça1.D7, R1.Pin_0, S1.Pin_1, S1.Pin_2
  N3: Parça1.5V, S1.Pin_3, S1.Pin_4

// code stored in the sketch: debouncing.ino
int inPin = 7;         	  // the number of the input pin
int outPin = 13;       	  // the number of the output pin

int counter = 0;       	  // how many times we have seen new value
int reading;           	  // the current value read from the input pin
int current_state = LOW;  // the debounced input value
int debounce_count = 10;  // number of millis/samples to consider before declaring a debounced input

void setup()
{
  pinMode(inPin, INPUT);
  pinMode(outPin, OUTPUT);
  digitalWrite(outPin, current_state); // setup the Output LED for initial state
}


void loop()
{
    reading = digitalRead(inPin);

    if(reading == current_state && counter > 0)
    {
      counter--;
    }
    if(reading != current_state)
    {
       counter++; 
    }
    if(counter >= debounce_count)
    {
      counter = 0;
      current_state = reading;
      digitalWrite(outPin, current_state);
    }
    delay(1)
}
